# Fritzing sketch Emeteur-NE555-CI-V1 (saved by Fritzing 0.9.3b)
circuit board: 5cm x 4.6cm
breadboards: 1

parts:
  R1 = Resistor [tolerance=±5% resistance=220 package=THT]
  R2 = Resistor [tolerance=±5% resistance=220 package=THT]
  R3 = Resistor [tolerance=±5% resistance=220 package=THT]
  R4 = Resistor [tolerance=±5% resistance=220 package=THT]
  R5 = Resistor [tolerance=±5% resistance=220 package=THT]
  R6 = Resistor [tolerance=±5% resistance=220 package=THT]
  R7 = Resistor [tolerance=±5% resistance=220 package=THT]
  R8 = Resistor [tolerance=±5% resistance=220 package=THT]
  C1 = Ceramic Capacitor [capacitance=100nF package="100 mil [THT, multilayer]"]
  C2 = Ceramic Capacitor [capacitance=100nF package="100 mil [THT, multilayer]"]
  C3 = Ceramic Capacitor [capacitance=100nF package="100 mil [THT, multilayer]"]
  C4 = Ceramic Capacitor [capacitance=100nF package="100 mil [THT, multilayer]"]
  IC1 = General purpose bipolar Timer [package=dil-08]
  C5 = Ceramic Capacitor [capacitance=100nF package="100 mil [THT, multilayer]"]

nets:
  N1: R1.Pin_0, R2.Pin_1, R3.Pin_1, R4.Pin_1, R5.Pin_1, R6.Pin_0, R7.Pin_0, R8.Pin_0, IC1.TRI
  N2: R1.Pin_1, R6.Pin_1, R7.Pin_1, R8.Pin_1, IC1.GND, IC1.CON
  N3: R2.Pin_0, R3.Pin_0, R4.Pin_0, R5.Pin_0, C1.1, C2.1, C3.1, C4.1, IC1.OUT, IC1.DIS
  N4: C1.0, C2.0, C3.0, C4.0
  N5: IC1._RES, C5.0
  N6: IC1.VCC+, C5.1

notes:
  +5
  GRD
  OUT
