# Fritzing sketch Emetteur_NE555_CI_V2 (saved by Fritzing 0.9.3b)
circuit board: 7.5cm x 4.5cm
breadboards: 1

parts:
  U1 = 555 Timer [package="DIP8 [THT]"]
  U2 = 555 Timer [package="DIP8 [THT]"]
  R1 = Resistor [tolerance=±5% resistance=220 package=THT]
  R2 = Resistor [tolerance=±5% resistance=220 package=THT]
  R3 = Resistor [tolerance=±5% resistance=220 package=THT]
  R5 = Resistor [tolerance=±5% resistance=220 package=THT]
  R6 = Resistor [tolerance=±5% resistance=220 package=THT]
  C1 = Electrolytic Capacitor [capacitance=1µF package="100 mil [THT, electrolytic]"]
  C2 = Electrolytic Capacitor [capacitance=1µF package="100 mil [THT, electrolytic]"]
  C3 = Electrolytic Capacitor [capacitance=1µF package="100 mil [THT, electrolytic]"]
  C4 = Tantalum Capacitor [capacitance=1μF package="100 mil [THT, tantalum]"]
  R7 = Resistor [tolerance=±5% resistance=220 package=THT]
  R8 = Resistor [tolerance=±5% resistance=220 package=THT]
  R9 = Resistor [tolerance=±5% resistance=220 package=THT]
  R10 = Resistor [tolerance=±5% resistance=220 package=THT]
  R11 = Resistor [tolerance=±5% resistance=220 package=THT]
  R12 = Resistor [tolerance=±5% resistance=220 package=THT]
  R13 = Resistor [tolerance=±5% resistance=220 package=THT]
  C5 = Electrolytic Capacitor [capacitance=1µF package="100 mil [THT, electrolytic]"]
  C6 = Electrolytic Capacitor [capacitance=1µF package="100 mil [THT, electrolytic]"]
  C7 = Electrolytic Capacitor [capacitance=1µF package="100 mil [THT, electrolytic]"]
  C8 = Tantalum Capacitor [capacitance=1μF package="100 mil [THT, tantalum]"]
  R14 = Resistor [tolerance=±5% resistance=220 package=THT]
  LED1 = LED - 5mm [color="Infrared (940nm)" package="5 mm [THT]"]

nets:
  N1: U1.Ground, U2.Ground, C3.+, C4.+, C7.+, C8.+, LED1.anode
  N2: U1.Trigger, U1.Threshold, R6.Pin_0, C1.-
  N3: U1.Output, U2.Reset, U2.Vcc_Supply_Voltage, R13.Pin_1
  N4: U1.Reset, U1.Vcc_Supply_Voltage, R7.Pin_1
  N5: U1.Control_Voltage, C4.-
  N6: U1.Discharge, R1.Pin_0, R3.Pin_1
  N7: U2.Trigger, R14.Pin_1
  N8: U2.Output, U2.Threshold, R8.Pin_0, C5.-
  N9: U2.Control_Voltage, C8.-
  N10: U2.Discharge, R10.Pin_1, R11.Pin_0
  N11: R1.Pin_1, R2.Pin_1
  N12: R2.Pin_0, R7.Pin_0
  N13: R3.Pin_0, R5.Pin_0
  N14: R5.Pin_1, R6.Pin_1
  N15: C1.+, C2.-
  N16: C2.+, C3.-
  N17: R8.Pin_1, R9.Pin_1
  N18: R9.Pin_0, R10.Pin_0
  N19: R11.Pin_1, R12.Pin_1
  N20: R12.Pin_0, R13.Pin_0
  N21: C5.+, C6.-
  N22: C6.+, C7.-
  N23: R14.Pin_0, LED1.cathode

notes:
  GND
  Vcc
  +--+
  +-
  -+
  R1:3K
  R2:10K
  C1:47n
  C2:10n
  R3:680
  R4:1.2k
  C3:10n
  C4:10n
  R5:220
