# Fritzing sketch Emetteur_NE555_CI_V3.2 (saved by Fritzing 0.9.3b)
circuit board: 5.89378cm x 3.72402cm
breadboards: 1

parts:
  U1 = 555 Timer [package="DIP8 [THT]"]
  U2 = 555 Timer [package="DIP8 [THT]"]
  R3 = Resistor [tolerance=±5% resistance=220 package=THT]
  C3 = Electrolytic Capacitor [capacitance=1µF package="100 mil [THT, electrolytic]"]
  C4 = Tantalum Capacitor [capacitance=1μF package="100 mil [THT, tantalum]"]
  R7 = Resistor [tolerance=±5% resistance=220 package=THT]
  R8 = Resistor [tolerance=±5% resistance=220 package=THT]
  R11 = Resistor [tolerance=±5% resistance=220 package=THT]
  C5 = Electrolytic Capacitor [capacitance=1µF package="100 mil [THT, electrolytic]"]
  C8 = Tantalum Capacitor [capacitance=1μF package="100 mil [THT, tantalum]"]
  R1 = Resistor [tolerance=±5% resistance=330 package=THT]
  C9 = Ceramic Capacitor [capacitance=100nF package="100 mil [THT, multilayer]"]
  C10 = Ceramic Capacitor [capacitance=100nF package="100 mil [THT, multilayer]"]

nets:
  N1: U1.Ground, U2.Ground, C3.+, C4.+, C5.+, C8.+, C9.1, C10.1
  N2: U1.Trigger, U1.Threshold, R3.Pin_0, C3.-
  N3: U1.Output, U2.Reset
  N4: U1.Reset, U1.Vcc_Supply_Voltage, U2.Vcc_Supply_Voltage, R7.Pin_1, R11.Pin_1
  N5: U1.Control_Voltage, C4.-, C9.0, C10.0
  N6: U1.Discharge, R3.Pin_1, R1.Pin_1
  N7: U2.Output, U2.Threshold, R8.Pin_0, C5.-
  N8: U2.Control_Voltage, C8.-
  N9: U2.Discharge, R8.Pin_1, R11.Pin_0
  N10: R7.Pin_0, R1.Pin_0

notes:
  GND
  Vcc
  +--+
  +-
  -+
  R1
  R2
  C1
  C2
  R3
  R4
  C3
  C4
  OUT
