# Fritzing sketch Emetteur_NE555_VS_V2 (saved by Fritzing 0.9.3b)
breadboards: 1

parts:
  NE555_n°1 = IC, DIP package, 8 pins [chip_label=IC]
  NE555_n°2 = IC, DIP package, 8 pins [chip_label=IC]
  R1 = Resistor [tolerance=±5% resistance=3k package=THT]
  R2 = Resistor [tolerance=±5% resistance=10k package=THT]
  C1 = Ceramic Capacitor [capacitance=47nF package="100 mil [THT, multilayer]"]
  C2 = Ceramic Capacitor [capacitance=10nF package="100 mil [THT, multilayer]"]
  R1² = Resistor [tolerance=±5% resistance=1.2k package=THT]
  R2² = Resistor [tolerance=±5% resistance=1k package=THT]
  C3 = Ceramic Capacitor [capacitance=10nF package="100 mil [THT, multilayer]"]
  C1² = Ceramic Capacitor [capacitance=0.1nF package="100 mil [THT, multilayer]"]
  R3 = Resistor [tolerance=±5% resistance=220 package=THT]
  part = LED - 5mm [color="Red (633nm)" package="5 mm [THT]"]

nets:
  GND: NE555_n°1.pin1, NE555_n°2.pin1, C1.0, C2.0, C3.0, C1².0, part.cathode
  N1: NE555_n°1.pin2, NE555_n°1.pin6, R2.Pin_1, C1.1
  N2: NE555_n°1.pin3, NE555_n°2.pin4
  5V: NE555_n°1.pin4, NE555_n°1.pin8, NE555_n°2.pin8, R1.Pin_0, R1².Pin_0
  N3: NE555_n°1.pin5, C2.1
  N4: NE555_n°1.pin7, R1.Pin_1, R2.Pin_0
  N5: NE555_n°2.pin2, NE555_n°2.pin6, R2².Pin_1, C1².1
  N6: NE555_n°2.pin3, R3.Pin_0
  N7: NE555_n°2.pin5, C3.1
  N8: NE555_n°2.pin7, R1².Pin_1, R2².Pin_0
  N9: R3.Pin_1, part.anode

notes:
  Porteuse 1.36
  Modulation 38
