# Fritzing sketch Passe bande-tl081-CI-V1 (saved by Fritzing 0.9.3b)
circuit board: 7.5cm x 4.4cm
breadboards: 1

parts:
  U1 = LM358 [package=dip08]
  R1 = Resistor [tolerance=±5% resistance=220 package=THT]
  R2 = Resistor [tolerance=±5% resistance=220 package=THT]
  R3 = Resistor [tolerance=±5% resistance=220 package=THT]
  R4 = Resistor [tolerance=±5% resistance=220 package=THT]
  R5 = Resistor [tolerance=±5% resistance=220 package=THT]
  R6 = Resistor [tolerance=±5% resistance=220 package=THT]
  R7 = Resistor [tolerance=±5% resistance=220 package=THT]
  R8 = Resistor [tolerance=±5% resistance=220 package=THT]
  C1 = Electrolytic Capacitor [capacitance=1µF package="100 mil [THT, electrolytic]"]
  C2 = Electrolytic Capacitor [capacitance=1µF package="100 mil [THT, electrolytic]"]
  C3 = Electrolytic Capacitor [capacitance=1µF package="100 mil [THT, electrolytic]"]
  C4 = Electrolytic Capacitor [capacitance=1µF package="100 mil [THT, electrolytic]"]
  C5 = Electrolytic Capacitor [capacitance=1µF package="100 mil [THT, electrolytic]"]
  C6 = Electrolytic Capacitor [capacitance=1µF package="100 mil [THT, electrolytic]"]
  R9 = Resistor [tolerance=±5% resistance=220 package=THT]
  R10 = Resistor [tolerance=±5% resistance=220 package=THT]
  R11 = Resistor [tolerance=±5% resistance=220 package=THT]
  R12 = Resistor [tolerance=±5% resistance=220 package=THT]
  D1 = Rectifier Diode [part_number=1N4001 package="300 mil [THT]"]
  C7 = Electrolytic Capacitor [capacitance=1µF package="100 mil [THT, electrolytic]"]
  R13 = Resistor [tolerance=±5% resistance=220 package=THT]

nets:
  N1: U1.G$1_-IN, C6.-, R12.Pin_0
  N2: U1.G$1_+IN, R8.Pin_1, C7.-, R13.Pin_1
  N3: U1.G$2_-IN, C3.-, R9.Pin_0, D1.anode
  N4: R1.Pin_1, R2.Pin_1
  N5: R2.Pin_0, R3.Pin_0
  N6: R3.Pin_1, R4.Pin_1
  N7: R4.Pin_0, R5.Pin_1, C1.+, C4.+
  N8: R5.Pin_0, R6.Pin_0
  N9: R6.Pin_1, R7.Pin_1
  N10: R7.Pin_0, R8.Pin_0
  N11: C1.-, C2.+
  N12: C2.-, C3.+
  N13: C4.-, C5.+
  N14: C5.-, C6.+
  N15: R9.Pin_1, R10.Pin_1
  N16: R10.Pin_0, R11.Pin_0
  N17: R11.Pin_1, R12.Pin_1
  N18: D1.cathode, C7.+, R13.Pin_0

notes:
  tl081
  IN
  Vcc-
  GND
  Vcc+
  OUT1
  R1
  R2
  C
  R3
  +--+
  -+
  +-
  OUT2
