# Fritzing sketch Passe bande-tl081-CI-V3 (saved by Fritzing 0.9.3b)
circuit board: 5.4cm x 3.1cm
breadboards: 1

parts:
  U1 = LM358 [package=dip08]
  R1 = Resistor [tolerance=±5% resistance=220 package=THT]
  R2 = Resistor [tolerance=±5% resistance=220 package=THT]
  R4 = Resistor [tolerance=±5% resistance=220 package=THT]
  R5 = Resistor [tolerance=±5% resistance=220 package=THT]
  R7 = Resistor [tolerance=±5% resistance=220 package=THT]
  R8 = Resistor [tolerance=±5% resistance=220 package=THT]
  R9 = Resistor [tolerance=±5% resistance=220 package=THT]
  D1 = Rectifier Diode [part_number=1N4001 package="300 mil [THT]"]
  R13 = Resistor [tolerance=±5% resistance=220 package=THT]
  C8 = Tantalum Capacitor [capacitance=1μF package="100 mil [THT, tantalum]"]
  C9 = Tantalum Capacitor [capacitance=1μF package="100 mil [THT, tantalum]"]
  C10 = Tantalum Capacitor [capacitance=1μF package="100 mil [THT, tantalum]"]
  C11 = Tantalum Capacitor [capacitance=1μF package="100 mil [THT, tantalum]"]
  C12 = Tantalum Capacitor [capacitance=1μF package="100 mil [THT, tantalum]"]
  C13 = Tantalum Capacitor [capacitance=1μF package="100 mil [THT, tantalum]"]
  C14 = Tantalum Capacitor [capacitance=1μF package="100 mil [THT, tantalum]"]

nets:
  N1: U1.G$1_-IN, R9.Pin_1, C13.+
  N2: U1.G$1_+IN, R8.Pin_0, R13.Pin_1, C14.-
  N3: U1.G$2_-IN, R9.Pin_0, D1.anode, C10.+
  N4: R1.Pin_1, R2.Pin_1
  N5: R2.Pin_0, R4.Pin_0
  N6: R4.Pin_1, R5.Pin_1, C8.-, C11.-
  N7: R5.Pin_0, R7.Pin_0
  N8: R7.Pin_1, R8.Pin_1
  N9: D1.cathode, R13.Pin_0, C14.+
  N10: C8.+, C9.-
  N11: C9.+, C10.-
  N12: C11.+, C12.+
  N13: C12.-, C13.-

notes:
  tl081
  IN
  Vcc-
  GND
  Vcc+
  OUT
  R1
  R2
  C
  R3
  +--+
  -+
  +-
